# Fritzing sketch bluetooth (saved by Fritzing 0.9.5d)

parts:
  Part1 = Arduino Uno (Rev3) - ICSP
  Part2 = Bluetooth HC-05
  R1 = Resistor [tolerance=±5% resistance=2.2k package=THT]
  R2 = Resistor [tolerance=±5% resistance=1k package="0805 [SMD]"]

nets:
  N1: Part1.D2, Part2.TXD
  N2: Part1.D3_PWM, R2.Pin_1
  5V: Part1.5V, Part2.VCC
  GND: Part1.GND, Part2.GND, R1.Pin_1
  N3: Part2.RXD, R1.Pin_0, R2.Pin_0
