# Fritzing sketch bluetooth_2 (saved by Fritzing 1.0.2b)

parts:
  Part1 = Arduino Uno (Rev3) - ICSP
  Part2 = Bluetooth HC-05
  R1 = Resistor [tolerance=±5% resistance=2.2k power=0.25W package=THT]
  R2 = Resistor [tolerance=±5% resistance=1k package="0805 [SMD]"]
  LED1 = LED - 5mm [color="Red (633nm)" current=0.030A package="5 mm [THT]"]
  R3 = Resistor [tolerance=±5% resistance=1k package="0805 [SMD]"]

nets:
  GND: Part1.GND, Part2.GND, R1.Pin_1, LED1.cathode
  N1: Part1.D13/SCK, R3.Pin_1
  N2: Part1.D2, Part2.TXD
  N3: Part1.D3_PWM, R2.Pin_1
  5V: Part1.5V, Part2.VCC
  N4: Part2.RXD, R1.Pin_0, R2.Pin_0
