# Fritzing sketch compass (saved by Fritzing 0.9.5d)

parts:
  Part1 = Arduino Uno (Rev3) - ICSP
  Part2 = HMC5883L Triple-axis Magnetometer [part_number=1746]

nets:
  N1: Part1.A4/SDA, Part2.SCL
  N2: Part1.A5/SCL, Part2.SDA
  5V: Part1.5V, Part2.VIN
  GND: Part1.GND, Part2.GND

custom parts:
  HMC5883L Triple-axis Magnetometer: A magnetometer can sense where the strongest magnetic force is coming from, generally used to detect magnetic north. We based this breakout on a popular and well loved magnetometer, the HMC5883L. This compact sensor uses I2C to communicate and its very easy to use. Since it's a 3.3V max chip, we added circuitry to make it 5V-safe logic and power, for easy use with either 3 or 5V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
