# Fritzing sketch distance_sensor (saved by Fritzing 0.9.5d)

parts:
  Part1 = HY-SRF05 Ultrasonic Rangefinder
  Part2 = Arduino Uno (Rev3) - ICSP

nets:
  VCC: Part1.Vcc, Part2.5V
  N1: Part1.Trig, Part2.D12/MISO
  N2: Part1.Echo, Part2.D13/SCK
  GND: Part1.GND, Part2.GND
