# Fritzing sketch encoders (saved by Fritzing 0.9.5d)
breadboards: 1

parts:
  Part1 = FC-03
  Part2 = FC-03
  Part3 = Arduino Uno (Rev3) - ICSP

nets:
  VCC: Part1.VCC, Part2.VCC, Part3.5V
  GND: Part1.GND, Part2.GND, Part3.GND
  N1: Part1.A0, Part3.D2
  N2: Part2.A0, Part3.D3_PWM

custom parts:
  FC-03: FC-03, LM393 IR Speed Sensor Encoder By Nandan
