# Fritzing sketch turtle_bot (saved by Fritzing 0.9.5d)
breadboards: 1

parts:
  Part2 = HY-SRF05 Ultrasonic Rangefinder
  Part3 = HMC5883L Triple-axis Magnetometer [part_number=1746]
  Part6 = FC-03
  Part7 = Arduino Uno (Rev3)
  IC2 = L293D [package=THT]
  M3 = DC Motor
  M4 = DC Motor
  Part8 = FC-03
  VCC1 = Battery block 9V
  S1 = Toggle Switch [package=THT]
  Part9 = Bluetooth HC-05
  R4 = Resistor [tolerance=±5% resistance=1k package="0805 [SMD]"]
  R3 = Resistor [tolerance=±5% resistance=2.2k package=THT]

nets:
  VCC: Part2.Vcc, Part3.VIN, Part6.VCC, Part7.5V, IC2.+V, Part8.VCC, Part9.VCC
  N1: Part2.Trig, Part7.D12/MISO
  N2: Part2.Echo, Part7.D13/SCK
  GND: Part2.GND, Part3.GND, Part6.GND, Part7.GND, IC2.0V, Part8.GND, S1.L2, Part9.GND, R3.Pin_1
  N3: Part3.SDA, Part7.A5/SCL
  N4: Part3.SCL, Part7.A4/SDA
  N5: Part6.A0, Part7.D3_PWM
  N6: Part7.D8, IC2.Enable_2
  N7: Part7.D9_PWM, IC2.In_3
  N8: Part7.D10_PWM/SS, IC2.In_4
  N9: Part7.D11_PWM/MOSI, R4.Pin_1, R3.Pin_0
  N10: Part7.D2, Part8.A0
  N11: Part7.D4, Part9.TXD
  N12: Part7.D5_PWM, IC2.Enable_1
  N13: Part7.D6_PWM, IC2.In_1
  N14: Part7.D7, IC2.In_2
  N15: Part7.VIN, VCC1.+
  N16: IC2.Out_1_(_Controlled_by_Enable_1_), M3.pin_2
  N17: IC2.Out_2_(_Controlled_by_Enable_1_), M3.pin_1
  N18: IC2.Out_3_(_Controlled_by_Enable_2_), M4.pin_2
  N19: IC2.Out_4_(_Controlled_by_Enable_2_), M4.pin_1
  N20: Part9.RXD, R4.Pin_0

custom parts:
  HMC5883L Triple-axis Magnetometer: A magnetometer can sense where the strongest magnetic force is coming from, generally used to detect magnetic north. We based this breakout on a popular and well loved magnetometer, the HMC5883L. This compact sensor uses I2C to communicate and its very easy to use. Since it's a 3.3V max chip, we added circuitry to make it 5V-safe logic and power, for easy use with either 3 or 5V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
  FC-03: FC-03, LM393 IR Speed Sensor Encoder By Nandan
